// Logisim project LAB02.circ as structural Verilog: 1 circuit, main circuit main
module main (
);

  wire and_1_out, and_2_out, and_3_out, and_4_out, and_5_out, and_6_out, and_7_out, and_8_out, and_9_out,
       and_10_out, and_11_out, and_12_out, and_13_out, and_14_out, and_15_out, and_16_out, and_17_out,
       dipswitch_1_sw1, dipswitch_1_sw2, dipswitch_1_sw3, not_1_out, not_2_out, not_3_out, not_4_out,
       not_5_out, not_6_out, not_7_out, not_8_out, not_9_out, not_10_out, not_11_out, not_12_out, not_13_out,
       not_14_out, not_15_out, not_16_out, not_17_out, not_18_out, not_19_out, not_20_out, not_21_out,
       not_22_out, or_1_out, or_2_out, or_3_out, or_4_out, or_5_out, or_6_out, or_7_out;

  and and_1 (and_1_out, not_1_out, not_2_out, not_3_out);
  not not_1 (not_1_out, dipswitch_1_sw1);
  not not_2 (not_2_out, dipswitch_1_sw2);
  or or_1 (or_1_out, and_1_out, and_2_out, and_3_out, and_4_out);
  and and_2 (and_2_out, dipswitch_1_sw1, not_4_out, dipswitch_1_sw3);
  not not_3 (not_3_out, dipswitch_1_sw3);
  not not_4 (not_4_out, dipswitch_1_sw2);
  and and_3 (and_3_out, not_5_out, dipswitch_1_sw2, dipswitch_1_sw3);
  not not_5 (not_5_out, dipswitch_1_sw1);
  and and_4 (and_4_out, dipswitch_1_sw1, dipswitch_1_sw2, not_6_out);
  not not_6 (not_6_out, dipswitch_1_sw3);
  and and_5 (and_5_out, not_7_out, not_8_out);
  not not_7 (not_7_out, dipswitch_1_sw1);
  not not_8 (not_8_out, dipswitch_1_sw2);
  or or_2 (or_2_out, and_5_out, and_6_out, and_7_out);
  and and_6 (and_6_out, not_9_out, dipswitch_1_sw3);
  not not_9 (not_9_out, dipswitch_1_sw2);
  and and_7 (and_7_out, not_10_out, dipswitch_1_sw3);
  not not_10 (not_10_out, dipswitch_1_sw1);
  not not_11 (not_11_out, dipswitch_1_sw2);
  DipSwitch #(.number(3)) dipswitch_1 (.sw1(dipswitch_1_sw1), .sw2(dipswitch_1_sw2), .sw3(dipswitch_1_sw3));
  or or_3 (or_3_out, not_11_out, and_8_out, and_9_out);
  and and_8 (and_8_out, not_12_out, dipswitch_1_sw3);
  not not_12 (not_12_out, dipswitch_1_sw1);
  _7_Segment_Display u_7_segment_display_1 (
    .g(or_7_out), .f(or_6_out), .a(or_1_out), .b(or_2_out), .e(or_5_out), .d(or_4_out), .c(or_3_out));  // open: dp
  and and_9 (and_9_out, dipswitch_1_sw1, not_13_out);
  not not_13 (not_13_out, dipswitch_1_sw3);
  and and_10 (and_10_out, dipswitch_1_sw1, dipswitch_1_sw2, not_14_out);
  not not_14 (not_14_out, dipswitch_1_sw3);
  or or_4 (or_4_out, and_10_out, and_11_out);
  and and_11 (and_11_out, not_15_out, dipswitch_1_sw3);
  not not_15 (not_15_out, dipswitch_1_sw2);
  and and_12 (and_12_out, dipswitch_1_sw1, dipswitch_1_sw2, dipswitch_1_sw3);
  or or_5 (or_5_out, and_12_out, and_13_out);
  and and_13 (and_13_out, not_16_out, not_17_out);
  not not_16 (not_16_out, dipswitch_1_sw2);
  not not_17 (not_17_out, dipswitch_1_sw3);
  or or_6 (or_6_out, dipswitch_1_sw3, and_14_out, and_15_out);
  and and_14 (and_14_out, not_18_out, not_19_out);
  not not_18 (not_18_out, dipswitch_1_sw1);
  not not_19 (not_19_out, dipswitch_1_sw2);
  and and_15 (and_15_out, dipswitch_1_sw1, dipswitch_1_sw2);
  or or_7 (or_7_out, not_20_out, and_16_out, and_17_out);
  not not_20 (not_20_out, dipswitch_1_sw2);
  not not_21 (not_21_out, dipswitch_1_sw1);
  and and_16 (and_16_out, not_21_out, dipswitch_1_sw3);
  and and_17 (and_17_out, dipswitch_1_sw1, not_22_out);
  not not_22 (not_22_out, dipswitch_1_sw3);
endmodule
