// Logisim project lab3.circ as structural Verilog: 5 circuits, main circuit main
module main (
);

  demux1to2 demux1to2_1 ();  // open: m, s, x, y
endmodule

module demux1to2 (
  input  m,
  input  s,
  output x,
  output y
);

  wire not_1_out;

  not not_1 (not_1_out, s);
  and and_1 (x, m, not_1_out);
  and and_2 (y, s, m);
endmodule

module mux2to1 (
  input  x,
  input  s,
  input  y,
  output m
);

  wire and_1_out, and_2_out, not_1_out;

  not not_1 (not_1_out, s);
  and and_1 (and_1_out, x, not_1_out);
  and and_2 (and_2_out, s, y);
  or or_1 (m, and_1_out, and_2_out);
endmodule

module demux1to6 (
  input  s0,
  input  s1,
  input  i0,
  input  s2,
  output m0,
  output m1,
  output m2,
  output m3,
  output m4,
  output m5
);

  wire demux1to2_1_x, demux1to2_1_y, demux1to2_2_x, demux1to2_2_y;

  demux1to2 demux1to2_1 (.m(i0), .s(s2), .x(demux1to2_1_x), .y(demux1to2_1_y));
  demux1to2 demux1to2_2 (.m(demux1to2_1_x), .s(s1), .x(demux1to2_2_x), .y(demux1to2_2_y));
  demux1to2 demux1to2_3 (.m(demux1to2_2_x), .s(s0), .x(m0), .y(m1));
  demux1to2 demux1to2_4 (.m(demux1to2_2_y), .s(s0), .x(m2), .y(m3));
  demux1to2 demux1to2_5 (.m(demux1to2_1_y), .s(s0), .x(m4), .y(m5));
endmodule

module mux6to1 (
  input  input0,
  input  input1,
  input  S1,
  input  input2,
  input  S0,
  input  input3,
  input  S2,
  input  input4,
  input  input5,
  output out1
);

  wire mux2to1_1_m, mux2to1_2_m, mux2to1_3_m, mux2to1_4_m;

  mux2to1 mux2to1_1 (.x(input0), .s(S0), .y(input1), .m(mux2to1_1_m));
  mux2to1 mux2to1_2 (.x(input2), .s(S0), .y(input3), .m(mux2to1_2_m));
  mux2to1 mux2to1_3 (.x(input4), .s(S0), .y(input5), .m(mux2to1_3_m));
  mux2to1 mux2to1_4 (.x(mux2to1_1_m), .s(S1), .y(mux2to1_2_m), .m(mux2to1_4_m));
  mux2to1 mux2to1_5 (.x(mux2to1_4_m), .s(S2), .y(mux2to1_3_m), .m(out1));
endmodule
