// Logisim project lab4.circ as structural Verilog: 5 circuits, main circuit main
module main (
  input  S,
  input  Clock,
  input  R,
  output notQ,
  output Q
);

  wire and_1_out, and_2_out;

  and and_1 (and_1_out, S, Clock);
  and and_2 (and_2_out, Clock, R);
  nor nor_1 (notQ, and_1_out, Q);
  nor nor_2 (Q, notQ, and_2_out);
endmodule

module dLatch (
  input  d,
  input  Clock,
  output notQ,
  output Q
);

  wire not_1_out;

  not not_1 (not_1_out, d);
  srLatch srlatch_1 (.S(d), .Clock(Clock), .R(not_1_out), .notQ(notQ), .Q(Q));
endmodule

module Dflipflop (
  input  d,
  input  Clock,
  output out_3,
  output out_4
);

  wire dlatch_1_q, not_1_out, not_2_out;

  not not_1 (not_1_out, Clock);
  not not_2 (not_2_out, not_1_out);
  dLatch dlatch_1 (.d(d), .Clock(not_1_out), .Q(dlatch_1_q));  // open: notQ
  dLatch dlatch_2 (.d(dlatch_1_q), .Clock(not_2_out), .notQ(out_3), .Q(out_4));
endmodule

module srLatch (
  input  S,
  input  Clock,
  input  R,
  output notQ,
  output Q
);

  wire and_1_out, and_2_out;

  and and_1 (and_1_out, S, Clock);
  and and_2 (and_2_out, Clock, R);
  nor nor_1 (notQ, and_1_out, Q);
  nor nor_2 (Q, notQ, and_2_out);
endmodule

module dLatchNosrLatch (
  input  d,
  input  Clock,
  output notQ,
  output Q
);

  wire nand_1_out, nand_2_out, not_1_out;

  not not_1 (not_1_out, d);
  nand nand_1 (nand_1_out, d, Clock);
  nand nand_2 (nand_2_out, Clock, not_1_out);
  nor nor_1 (notQ, nand_1_out, Q);
  nor nor_2 (Q, notQ, nand_2_out);
endmodule
