// Logisim project lab5.circ as structural Verilog: 2 circuits, main circuit main
module main (
  input  in_1
);

  wire and_1_out, and_2_out, and_3_out, and_4_out, and_5_out, and_6_out, and_7_out, and_8_out, and_9_out,
       and_10_out, and_11_out, and_12_out, button_1_out, d_ff_1_q, d_ff_2_q, d_ff_3_q, d_ff_4_q, not_1_out,
       not_2_out, not_3_out, not_4_out, or_1_out, or_2_out, or_3_out, or_4_out;

  Button button_1 (.out(button_1_out));
  and and_1 (and_1_out, or_2_out, button_1_out);
  and and_2 (and_2_out, or_3_out, button_1_out);
  and and_3 (and_3_out, or_4_out, button_1_out);
  and and_4 (and_4_out, or_1_out, button_1_out);
  D_Flip_Flop d_ff_1 (.D(and_1_out), .clk(button_1_out), .Q(d_ff_1_q), .reset(in_1));  // open: Qn, preset
  D_Flip_Flop d_ff_2 (.D(and_2_out), .clk(button_1_out), .Q(d_ff_2_q), .reset(in_1));  // open: Qn, preset
  D_Flip_Flop d_ff_3 (.D(and_3_out), .clk(button_1_out), .Q(d_ff_3_q), .reset(in_1));  // open: Qn, preset
  D_Flip_Flop d_ff_4 (.D(and_4_out), .clk(button_1_out), .Q(d_ff_4_q), .reset(in_1));  // open: Qn, preset
  and and_5 (and_5_out, d_ff_1_q, d_ff_3_q);
  and and_6 (and_6_out, d_ff_3_q, d_ff_4_q);
  or or_1 (or_1_out, and_5_out, and_6_out);
  not not_1 (not_1_out, d_ff_4_q);
  not not_2 (not_2_out, d_ff_2_q);
  not not_3 (not_3_out, d_ff_4_q);
  and and_7 (and_7_out, d_ff_1_q, d_ff_2_q, d_ff_3_q, d_ff_4_q);
  and and_8 (and_8_out, not_1_out, d_ff_3_q);
  and and_9 (and_9_out, not_2_out, not_3_out);
  and and_10 (and_10_out, d_ff_2_q, d_ff_4_q);
  not not_4 (not_4_out, d_ff_1_q);
  LED led_1 (.in(and_7_out));
  or or_2 (or_2_out, and_8_out, and_9_out);
  or or_3 (or_3_out, d_ff_1_q, and_10_out);
  and and_11 (and_11_out, d_ff_2_q, not_4_out);
  and and_12 (and_12_out, d_ff_1_q, d_ff_3_q);
  or or_4 (or_4_out, and_11_out, and_12_out);
endmodule

module part2 (
);

  wire and_1_out, and_2_out, and_3_out, and_4_out, and_5_out, and_6_out, and_7_out, and_8_out, and_9_out,
       and_10_out, and_11_out, d_ff_1_q, d_ff_2_q, d_ff_3_q, d_ff_4_q, not_1_out, not_2_out, not_3_out,
       not_4_out, not_5_out, not_6_out, not_7_out, not_8_out, not_9_out, not_10_out, not_11_out, or_1_out,
       or_2_out, or_3_out, or_4_out, or_5_out, PenButton_out, Reset_out;

  Button Reset (.out(Reset_out));
  Button PenButton (.out(PenButton_out));
  D_Flip_Flop d_ff_1 (.D(or_2_out), .clk(PenButton_out), .Q(d_ff_1_q), .reset(Reset_out));  // open: Qn, preset
  D_Flip_Flop d_ff_2 (.D(or_3_out), .clk(PenButton_out), .Q(d_ff_2_q), .reset(Reset_out));  // open: Qn, preset
  D_Flip_Flop d_ff_3 (.D(or_4_out), .clk(PenButton_out), .Q(d_ff_3_q), .reset(Reset_out));  // open: Qn, preset
  D_Flip_Flop d_ff_4 (.D(or_1_out), .clk(PenButton_out), .Q(d_ff_4_q), .reset(Reset_out));  // open: Qn, preset
  and and_1 (and_1_out, d_ff_1_q, d_ff_3_q);
  and and_2 (and_2_out, d_ff_3_q, d_ff_4_q);
  not not_1 (not_1_out, d_ff_1_q);
  not not_2 (not_2_out, d_ff_2_q);
  not not_3 (not_3_out, d_ff_3_q);
  or or_1 (or_1_out, and_1_out, and_2_out);
  not not_4 (not_4_out, d_ff_1_q);
  not not_5 (not_5_out, d_ff_2_q);
  not not_6 (not_6_out, d_ff_1_q);
  not not_7 (not_7_out, d_ff_4_q);
  not not_8 (not_8_out, d_ff_2_q);
  not not_9 (not_9_out, d_ff_4_q);
  not not_10 (not_10_out, d_ff_4_q);
  and and_3 (and_3_out, not_1_out, not_2_out, not_3_out, d_ff_4_q);
  and and_4 (and_4_out, not_4_out, not_5_out, d_ff_3_q, d_ff_4_q);
  and and_5 (and_5_out, not_6_out, d_ff_2_q, d_ff_3_q, d_ff_4_q);
  and and_6 (and_6_out, d_ff_1_q, d_ff_2_q, d_ff_3_q, d_ff_4_q);
  and and_7 (and_7_out, not_7_out, d_ff_3_q);
  and and_8 (and_8_out, not_8_out, not_9_out);
  and and_9 (and_9_out, d_ff_2_q, not_10_out);
  or or_2 (or_2_out, and_7_out, and_8_out);
  or or_3 (or_3_out, d_ff_1_q, and_9_out);
  not not_11 (not_11_out, d_ff_1_q);
  and and_10 (and_10_out, d_ff_2_q, d_ff_3_q);
  and and_11 (and_11_out, d_ff_2_q, not_11_out);
  or or_4 (or_4_out, and_11_out, and_10_out);
  or or_5 (or_5_out, and_3_out, and_4_out, and_5_out, and_6_out);
  LED led_1 (.in(or_5_out));
endmodule
