// Logisim project lab6.circ as structural Verilog: 1 circuit, main circuit main
module main (
  input  CLK,
  input  enable,
  input  [3:0] Data,
  input  [1:0] wselect,
  input  [1:0] rselect,
  output [3:0] out_6
);

  wire demultiplexer_1_out0, demultiplexer_1_out1, demultiplexer_1_out2, demultiplexer_1_out3, reset_out;
  wire [3:0] demultiplexer_2_out0, demultiplexer_2_out1, demultiplexer_2_out2, demultiplexer_2_out3, R0_q,
       R1_q, R2_q, R3_q;

  Demultiplexer #(.enable("false"), .select(2)) demultiplexer_1 (
    .out0(demultiplexer_1_out0), .out1(demultiplexer_1_out1), .out2(demultiplexer_1_out2),
    .out3(demultiplexer_1_out3), .in(enable), .sel(wselect));
  Demultiplexer #(.enable("false"), .select(2), .width(4)) demultiplexer_2 (
    .out0(demultiplexer_2_out0), .out1(demultiplexer_2_out1), .out2(demultiplexer_2_out2),
    .out3(demultiplexer_2_out3), .in(Data), .sel(wselect));
  Button reset (.out(reset_out));
  Register #(.width(4)) R0 (.D(demultiplexer_2_out0), .en(demultiplexer_1_out0), .clk(CLK), .Q(R0_q), .clr(reset_out));
  Register #(.width(4)) R1 (.D(demultiplexer_2_out1), .en(demultiplexer_1_out1), .clk(CLK), .Q(R1_q), .clr(reset_out));
  Register #(.width(4)) R2 (.D(demultiplexer_2_out2), .en(demultiplexer_1_out2), .clk(CLK), .Q(R2_q), .clr(reset_out));
  Register #(.width(4)) R3 (.D(demultiplexer_2_out3), .en(demultiplexer_1_out3), .clk(CLK), .Q(R3_q), .clr(reset_out));
  Multiplexer #(.enable("false"), .select(2), .width(4)) multiplexer_1 (
    .in0(R0_q), .in1(R1_q), .in2(R2_q), .in3(R3_q), .out(out_6), .sel(rselect));
endmodule
